# Fritzing sketch rc_controller (saved by Fritzing 0.9.3b)

parts:
  U1 = LCD-16X2 [package=lcd-16x2]
  Bauteil2 = NRF24L01+ Breakout Board
  BAT1 = Battery Holders [package=lipo-1100mAh]
  R1 = Resistor [tolerance=±5% resistance=10k package="2010 [SMD]"]
  R2 = Resistor [tolerance=±5% resistance=10k package="2010 [SMD]"]
  U2 = POT [package=pot_mammoth]
  U3 = POT [package=pot_mammoth]
  U4 = POT [package=pot_mammoth]
  U5 = POT [package=pot_mammoth]
  U6 = POT [package=pot_mammoth]
  U7 = POT [package=pot_mammoth]
  Bauteil1 = Arduino Mega 2560 (Rev3)
  C1 = Electrolytic Capacitor [capacitance=10μF package="0605 [SMD, electrolytic]"]
  S1 = Square Pushbutton
  S2 = Square Pushbutton
  S3 = Square Pushbutton
  S4 = Square Pushbutton
  Bauteil3 = Bluetooth HC-05 Macho
  R3 = Trimmer Potentiometer [maximum_resistance=10kΩ package=THT]  # not connected

nets:
  N1: U1.RS, Bauteil1.D13_PWM
  N2: U1.E, Bauteil1.D12_PWM
  N3: U1.DB0, Bauteil1.D8_PWM
  N4: U1.DB1, Bauteil1.D9_PWM
  N5: U1.DB2, Bauteil1.D10_PWM
  N6: U1.DB3, Bauteil1.D11_PWM
  N7: U1.DB4, Bauteil1.D4_PWM
  N8: U1.DB5, Bauteil1.D5_PWM
  N9: U1.DB6, Bauteil1.D6_PWM
  N10: U1.DB7, Bauteil1.D7_PWM
  GND: Bauteil2.GND, BAT1.-, R1.Pin_0, U2.S, U3.S, U4.S, U5.S, U6.S, U7.S, Bauteil1.GND, C1.-, S1.leg0, S2.leg0, S3.leg0, S4.leg0, Bauteil3.GND
  VCC: Bauteil2.VCC, Bauteil1.3V3, C1.+
  N11: Bauteil2.CE, Bauteil1.D2_PWM
  N12: Bauteil2.CS, Bauteil1.D3_PWM
  N13: Bauteil2.SCK, Bauteil1.D52
  N14: Bauteil2.MOSI, Bauteil1.D51
  N15: Bauteil2.MISO, Bauteil1.D50
  N16: BAT1.+, R2.Pin_1, Bauteil1.VIN
  N17: R1.Pin_1, R2.Pin_0, Bauteil1.A0
  N18: U2.A, Bauteil1.A1
  5V: U2.E, U3.E, U4.E, U5.E, U6.E, U7.E, Bauteil1.5V, Bauteil3.VCC
  N19: U3.A, Bauteil1.A2
  N20: U4.A, Bauteil1.A3
  N21: U5.A, Bauteil1.A4
  N22: U6.A, Bauteil1.A5
  N23: U7.A, Bauteil1.A6
  N24: Bauteil1.D21/SCL, S4.leg1
  N25: Bauteil1.D20/SDA, Bauteil1.SDA, S3.leg1
  N26: Bauteil1.D19/RX1, S1.leg1
  N27: Bauteil1.D18/TX1, S2.leg1
  N28: Bauteil1.D17_PWM/RX2, Bauteil3.TXD
  N29: Bauteil1.D16_PWM/TX2, Bauteil3.RXD
